# Fritzing sketch ArduinoTeensy (saved by Fritzing 0.9.3b)
breadboards: 1

parts:
  Part1 = Arduino Uno (Rev3)
  Teensy_3_2 = Teensy 3.1
  U1 = BNC [package=bnc]

nets:
  GND: Part1.GND, Teensy_3_2.GND, U1.GND
  N1: Part1.D4, U1.OUT
  N2: Part1.D5_PWM, Teensy_3_2.D4
  N3: Part1.D6_PWM, Teensy_3_2.D3
